# Fritzing sketch Mini Project (saved by Fritzing 0.9.4)
breadboards: 1

parts:
  Part1 = Adafruit ItsyBitsy M4 [part_number="Adafruit #3800"]
  Part2 = Adafruit 1.44 inch TFT Breakout [part_number="Adafruit #2088"]
  Piezo1 = Piezo Speaker - PC Mount [part_number=COM-07950]
  M1 = Dagu DGServo 9g (Top view) [part_number=RS001B]
  M2 = Dagu DGServo 9g (Top view) [part_number=RS001B]
  M3 = Dagu DGServo 9g (Top view) [part_number=RS001B]
  M4 = Dagu DGServo 9g (Top view) [part_number=RS001B]
  HC-SR04_Sensor_1 = HC-SR04 Ultrasonic Distance Sensor
  R1 = Resistor [tolerance=±5% resistance=10k package="0402 [SMD]"]
  R2 = Resistor [tolerance=±5% resistance=10k package="0402 [SMD]"]

nets:
  N1: Part1.D3, HC-SR04_Sensor_1.TRIG
  N2: Part1.D4, R1.Pin_1, R2.Pin_1
  GND: Part1.GND, Part2.GND, Piezo1.GND, M1.gnd, M2.gnd, M3.gnd, M4.gnd, HC-SR04_Sensor_1.GND, R2.Pin_0
  N3: Part1.D13, M3.pulse
  N4: Part1.D12, M4.pulse
  N5: Part1.D11, M2.pulse
  N6: Part1.D10, Part2.TFTCS
  N7: Part1.D9, Part2.TFTDC
  N8: Part1.D7, Part2.RESET
  N9: Part1.D5_5V, M1.pulse
  N10: Part1.MISO, Part2.MISO
  N11: Part1.MOSI, Part2.MOSI
  N12: Part1.SCK, Part2.SCK
  N13: Part1.A5, Part2.LITE
  N14: Part1.A0, Piezo1.VCC
  VCC: Part1.+3V3, Part2.VIN, M1.vcc, M2.vcc, M3.vcc, M4.vcc, HC-SR04_Sensor_1.VCC
  N15: HC-SR04_Sensor_1.ECHO, R1.Pin_0

custom parts:
  Adafruit ItsyBitsy M4: What's smaller than a Feather but larger than a Trinket? It's an Adafruit ItsyBitsy M4 Express featuring the Microchip ATSAMD51! Small, powerful, with a ultra fast ATSAMD51 Cortex M4 processor running at 120 MHz - this microcontroller board is perfect when you want something very compact, with a ton of horsepower and a bunch of pins. This Itsy is like a bullet train, with it's 120MHz Cortex M4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
  Adafruit 1.44 inch TFT Breakout: This lovely little display breakout is the best way to add a small, colorful and bright display to any project. Since the display uses 4-wire SPI to communicate and has its own pixel-addressable frame buffer, it can be used with every kind of microcontroller. Even a very small one with low memory and few pins available! The 1.44" display has 128x128 color pixels. Unlike the low cost "Nokia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
  Piezo Speaker - PC Mount: This is a small 12mm round speaker that operates around the audible 2kHz range. You can use these speakers to create simple music or user interfaces. Each speaker is PTH solderable and requires an operating voltage of 3.5-5V with a mean current of 35mA max. These speakers also have a typical sound output of 95 dBA and a coil resistance of 42 ±6.3 ohms.
